# Fritzing sketch Webasto WBus Arduino Serial Interface mk7 (saved by Fritzing 0.9.1b)
circuit board: 3cm x 3cm
stripboards: 1

parts:
  BC1 = NPN-Transistor [part_number="BC548 NPN" package="TO92 [THT]"]
  BC3 = NPN-Transistor [part_number="BC548 NPN" package="TO92 [THT]"]
  Q1 = PNP-Transistor [part_number="BC557 PNP" package="TO92 [THT]"]
  J1 = female pin header, 6 pins [form="♀ (female)" part_number="FTDI BASIC"]
  3_pin_header_to_heater = female pin header, 3 pins [form="♀ (female)"]
  R1 = Resistor [tolerance=±5% resistance=10k package=THT]
  R3 = Resistor [tolerance=±5% resistance=1k package=THT]
  R7 = Resistor [tolerance=±5% resistance=10k package=THT]
  R8 = Resistor [tolerance=±5% resistance=10k package=THT]
  R9 = Resistor [tolerance=±5% resistance=1k package=THT]
  LED1 = LED - 3mm [color="Yellow (595nm)" package="3 mm [THT]"]
  R10 = Resistor [tolerance=±5% resistance=10k package=THT]
  R5 = Resistor [tolerance=±5% resistance=1k package=THT]
  BC2 = NPN-Transistor [part_number="BC548 NPN" package="TO92 [THT]"]

nets:
  N1: BC1.C, J1.pin2, R7.Pin_1
  N2: BC1.B, R9.Pin_0
  GND: BC1.E, BC3.E, J1.pin6, 3_pin_header_to_heater.pin2, LED1.cathode, BC2.E
  WBUS: BC3.C, 3_pin_header_to_heater.pin3, R3.Pin_1, R10.Pin_1
  N3: BC3.B, R1.Pin_1
  N4: Q1.E, 3_pin_header_to_heater.pin1, R3.Pin_0
  N5: Q1.B, R10.Pin_0
  N6: Q1.C, R9.Pin_1, R5.Pin_0
  N7: J1.pin3, BC2.B
  N8: J1.pin4, R7.Pin_0, R8.Pin_0
  N9: R1.Pin_0, R8.Pin_1, BC2.C
  N10: LED1.anode, R5.Pin_1

notes:
  Webasto WBUS to 5v Serial TTL interface
  Note hidden cuts under transistors!!
  Copy & paste the strip board for locations of cuts without components!
  3 pin connector
  wbus / GND / 12v
  6 pin connector
  DTR / RX / TX /5V /CTS /Gnd
  +12v
  Webasto WBUS interface 12v to 5v TTL interface
  https://github.com/stuartpittaway/WebastoWBUSInterface
  WBUS Interface

custom parts:
  NPN-Transistor: A standard NPN-transistor
